// Logisim project MainFile.circ as structural Verilog
module Symmetry_4b_0 (
  input  x1,
  input  x2,
  input  x3,
  input  x4,
  output f
);

  nor nor_1 (f, x1, x2, x3, x4);
endmodule

module Symmetry_4b_1 (
  input  x1,
  input  x2,
  input  x3,
  input  x4,
  output f
);

  ExactlyOne xor_1 (.out(f), .in0(x1), .in1(x2), .in2(x3), .in3(x4));
endmodule

module Symmetry_4b_2 (
  input  x1,
  input  x2,
  input  x3,
  input  x4,
  output f
);

  wire symmetry_4b_0_1_f, symmetry_4b_1_1_f, symmetry_4b_3_1_f, symmetry_4b_4_1_f;

  Symmetry_4b_0 symmetry_4b_0_1 (.x1(x1), .x2(x2), .x3(x3), .x4(x4), .f(symmetry_4b_0_1_f));
  Symmetry_4b_1 symmetry_4b_1_1 (.x1(x1), .x2(x2), .x3(x3), .x4(x4), .f(symmetry_4b_1_1_f));
  Symmetry_4b_3 symmetry_4b_3_1 (.x1(x1), .x2(x2), .x3(x3), .x4(x4), .f(symmetry_4b_3_1_f));
  Symmetry_4b_4 symmetry_4b_4_1 (.x1(x1), .x2(x2), .x3(x3), .x4(x4), .f(symmetry_4b_4_1_f));
  nor nor_1 (f, symmetry_4b_0_1_f, symmetry_4b_1_1_f, symmetry_4b_3_1_f, symmetry_4b_4_1_f);
endmodule

module Symmetry_4b_3 (
  input  x1,
  input  x2,
  input  x3,
  input  x4,
  output f
);

  ExactlyOne xor_1 (.out(f), .in0(x1), .in1(x2), .in2(x3), .in3(x4));
endmodule

module Symmetry_4b_4 (
  input  x1,
  input  x2,
  input  x3,
  input  x4,
  output f
);

  and and_1 (f, x1, x2, x3, x4);
endmodule
